// Logisim project Project Circuit.circ as structural Verilog: 1 circuit, main circuit main
module main (
  input  A,
  input  B,
  input  C,
  input  D,
  input  E,
  input  F,
  input  G,
  input  H
);

  wire and_1_out, nand_1_out, nand_2_out, not_1_out, xnor_1_out, xnor_2_out, xnor_3_out, xor_1_out, xor_2_out;

  xnor xnor_1 (xnor_1_out, A, B);
  nand nand_1 (nand_1_out, C, D);
  nand nand_2 (nand_2_out, E, F);
  xnor xnor_2 (xnor_2_out, G, H);
  xor xor_1 (xor_1_out, xnor_1_out, nand_1_out);
  xor xor_2 (xor_2_out, nand_2_out, xnor_2_out);
  xnor xnor_3 (xnor_3_out, xor_1_out, xor_2_out);
  not not_1 (not_1_out, xnor_3_out);
  and and_1 (and_1_out, xor_1_out, not_1_out);
  // Probe on and_1_out
endmodule
